// Logisim project ex1.circ as structural Verilog: 1 circuit, main circuit non_pipelined
module non_pipelined (
  input  [7:0] in1,
  input  [7:0] in2,
  input  CLK,
  output [7:0] out1
);

  wire [7:0] adder_1_out, multiplier_1_out, register_1_q;

  Multiplier multiplier_1 (.a(in1), .b(in2), .out(multiplier_1_out));  // open: cin, cout
  Register register_1 (.D(multiplier_1_out), .en(1'b1), .clk(CLK), .Q(register_1_q));  // open: clr
  Adder adder_1 (.a(register_1_q), .b(out1), .out(adder_1_out));  // open: cin, cout
  Register register_2 (.D(adder_1_out), .en(1'b1), .clk(CLK), .Q(out1));  // open: clr
endmodule
