// Logisim project regfile.circ as structural Verilog: 1 circuit, main circuit regfile
module regfile (
  input  [4:0] rs1,
  input  [4:0] rs2,
  input  [4:0] rd,
  input  [31:0] Write_Data,
  input  RegWEn,
  input  clk,
  output [31:0] ra,
  output [31:0] sp,
  output [31:0] t0,
  output [31:0] t1,
  output [31:0] t2,
  output [31:0] s0,
  output [31:0] s1,
  output [31:0] a0,
  output [31:0] Read_Data_1,
  output [31:0] Read_Data_2
);

  wire decoder_1_out1, decoder_1_out2, decoder_1_out3, decoder_1_out4, decoder_1_out5, decoder_1_out6,
       decoder_1_out7, decoder_1_out8, decoder_1_out9, decoder_1_out10, decoder_1_out11, decoder_1_out12,
       decoder_1_out13, decoder_1_out14, decoder_1_out15, decoder_1_out16, decoder_1_out17, decoder_1_out18,
       decoder_1_out19, decoder_1_out20, decoder_1_out21, decoder_1_out22, decoder_1_out23, decoder_1_out24,
       decoder_1_out25, decoder_1_out26, decoder_1_out27, decoder_1_out28, decoder_1_out29, decoder_1_out30,
       decoder_1_out31;
  wire [31:0] w0, w1, w2, w3, w4, w5, w6, w7, w8, w9, w10, w11, w12, w13, w14, w15, w16, w17, w18, w19, w20,
       w21, w22, w23, w24, w25, w26, w27, w28, w29, w30, w31, x3, x4, x11, x12, x13, x14, x15, x16, x17, x18,
       x19, x20, x21, x22, x23, x24, x25, x26, x27, x28, x29, x30, x31;

  Register #(.width(32)) register_1 (.D(w8), .en(decoder_1_out8), .clk(clk), .Q(s0));  // open: clr
  Register #(.width(32)) register_2 (.D(w16), .en(decoder_1_out16), .clk(clk), .Q(x16));  // open: clr
  Register #(.width(32)) register_3 (.D(w24), .en(decoder_1_out24), .clk(clk), .Q(x24));  // open: clr
  Register #(.width(32)) register_4 (.D(w1), .en(decoder_1_out1), .clk(clk), .Q(ra));  // open: clr
  Register #(.width(32)) register_5 (.D(w9), .en(decoder_1_out9), .clk(clk), .Q(s1));  // open: clr
  Decoder #(.select(5)) decoder_1 (
    .out1(decoder_1_out1), .out2(decoder_1_out2), .out3(decoder_1_out3), .out4(decoder_1_out4),
    .out5(decoder_1_out5), .out6(decoder_1_out6), .out7(decoder_1_out7), .out8(decoder_1_out8),
    .out9(decoder_1_out9), .out10(decoder_1_out10), .out11(decoder_1_out11), .out12(decoder_1_out12),
    .out13(decoder_1_out13), .out14(decoder_1_out14), .out15(decoder_1_out15), .out16(decoder_1_out16),
    .out17(decoder_1_out17), .out18(decoder_1_out18), .out19(decoder_1_out19), .out20(decoder_1_out20),
    .out21(decoder_1_out21), .out22(decoder_1_out22), .out23(decoder_1_out23), .out24(decoder_1_out24),
    .out25(decoder_1_out25), .out26(decoder_1_out26), .out27(decoder_1_out27), .out28(decoder_1_out28),
    .out29(decoder_1_out29), .out30(decoder_1_out30), .out31(decoder_1_out31), .sel(rd), .en(RegWEn));  // open: out0
  Register #(.width(32)) register_6 (.D(w17), .en(decoder_1_out17), .clk(clk), .Q(x17));  // open: clr
  Register #(.width(32)) register_7 (.D(w25), .en(decoder_1_out25), .clk(clk), .Q(x25));  // open: clr
  Register #(.width(32)) register_8 (.D(w2), .en(decoder_1_out2), .clk(clk), .Q(sp));  // open: clr
  Register #(.width(32)) register_9 (.D(w10), .en(decoder_1_out10), .clk(clk), .Q(a0));  // open: clr
  Register #(.width(32)) register_10 (.D(w18), .en(decoder_1_out18), .clk(clk), .Q(x18));  // open: clr
  Register #(.width(32)) register_11 (.D(w26), .en(decoder_1_out26), .clk(clk), .Q(x26));  // open: clr
  Register #(.width(32)) register_12 (.D(w3), .en(decoder_1_out3), .clk(clk), .Q(x3));  // open: clr
  Register #(.width(32)) register_13 (.D(w11), .en(decoder_1_out11), .clk(clk), .Q(x11));  // open: clr
  Register #(.width(32)) register_14 (.D(w19), .en(decoder_1_out19), .clk(clk), .Q(x19));  // open: clr
  Register #(.width(32)) register_15 (.D(w27), .en(decoder_1_out27), .clk(clk), .Q(x27));  // open: clr
  Register #(.width(32)) register_16 (.D(w4), .en(decoder_1_out4), .clk(clk), .Q(x4));  // open: clr
  Register #(.width(32)) register_17 (.D(w12), .en(decoder_1_out12), .clk(clk), .Q(x12));  // open: clr
  Register #(.width(32)) register_18 (.D(w20), .en(decoder_1_out20), .clk(clk), .Q(x20));  // open: clr
  Register #(.width(32)) register_19 (.D(w28), .en(decoder_1_out28), .clk(clk), .Q(x28));  // open: clr
  Register #(.width(32)) register_20 (.D(w5), .en(decoder_1_out5), .clk(clk), .Q(t0));  // open: clr
  Register #(.width(32)) register_21 (.D(w13), .en(decoder_1_out13), .clk(clk), .Q(x13));  // open: clr
  Register #(.width(32)) register_22 (.D(w21), .en(decoder_1_out21), .clk(clk), .Q(x21));  // open: clr
  Register #(.width(32)) register_23 (.D(w29), .en(decoder_1_out29), .clk(clk), .Q(x29));  // open: clr
  Register #(.width(32)) register_24 (.D(w6), .en(decoder_1_out6), .clk(clk), .Q(t1));  // open: clr
  Register #(.width(32)) register_25 (.D(w14), .en(decoder_1_out14), .clk(clk), .Q(x14));  // open: clr
  Register #(.width(32)) register_26 (.D(w22), .en(decoder_1_out22), .clk(clk), .Q(x22));  // open: clr
  Register #(.width(32)) register_27 (.D(w30), .en(decoder_1_out30), .clk(clk), .Q(x30));  // open: clr
  Register #(.width(32)) register_28 (.D(w7), .en(decoder_1_out7), .clk(clk), .Q(t2));  // open: clr
  Register #(.width(32)) register_29 (.D(w15), .en(decoder_1_out15), .clk(clk), .Q(x15));  // open: clr
  Register #(.width(32)) register_30 (.D(w23), .en(decoder_1_out23), .clk(clk), .Q(x23));  // open: clr
  Register #(.width(32)) register_31 (.D(w31), .en(decoder_1_out31), .clk(clk), .Q(x31));  // open: clr
  Multiplexer #(.select(5), .width(32)) multiplexer_1 (
    .in0({32{1'b0}}), .in1(ra), .in2(sp), .in3(x3), .in4(x4), .in5(t0), .in6(t1), .in7(t2), .in8(s0),
    .in9(s1), .in10(a0), .in11(x11), .in12(x12), .in13(x13), .in14(x14), .in15(x15), .in16(x16), .in17(x17),
    .in18(x18), .in19(x19), .in20(x20), .in21(x21), .in22(x22), .in23(x23), .in24(x24), .in25(x25),
    .in26(x26), .in27(x27), .in28(x28), .in29(x29), .in30(x30), .in31(x31), .out(Read_Data_1), .sel(rs1));  // open: en
  Multiplexer #(.select(5), .width(32)) multiplexer_2 (
    .in0({32{1'b0}}), .in1(ra), .in2(sp), .in3(x3), .in4(x4), .in5(t0), .in6(t1), .in7(t2), .in8(s0),
    .in9(s1), .in10(a0), .in11(x11), .in12(x12), .in13(x13), .in14(x14), .in15(x15), .in16(x16), .in17(x17),
    .in18(x18), .in19(x19), .in20(x20), .in21(x21), .in22(x22), .in23(x23), .in24(x24), .in25(x25),
    .in26(x26), .in27(x27), .in28(x28), .in29(x29), .in30(x30), .in31(x31), .out(Read_Data_2), .sel(rs2));  // open: en
  Demultiplexer #(.select(5), .width(32)) demultiplexer_1 (
    .out0(w0), .out1(w1), .out2(w2), .out3(w3), .out4(w4), .out5(w5), .out6(w6), .out7(w7), .out8(w8),
    .out9(w9), .out10(w10), .out11(w13), .out12(w12), .out13(x13), .out14(w14), .out15(w15), .out16(w16),
    .out17(w17), .out18(w18), .out19(w19), .out20(w20), .out21(w21), .out22(w22), .out23(w23), .out24(w24),
    .out25(w25), .out26(w26), .out27(w27), .out28(w28), .out29(w29), .out30(w30), .out31(w31),
    .in(Write_Data), .sel(rd));  // open: en

  // Other names for the same wires on the sheet: read_data1[31:0] = Read_Data_1; read_data2[31:0] = Read_Data_2;
  //   read_reg1[4:0] = rs1; read_reg2[4:0] = rs2; write_en = RegWEn; write_reg[4:0] = rd; x1[31:0] = ra;
  //   x2[31:0] = sp; x5[31:0] = t0; x6[31:0] = t1; x7[31:0] = t2; x8[31:0] = s0; x9[31:0] = s1; x10[31:0] = a0

  // Notes on the sheet:
  //   INPUTS to your circuit
  //   DON'T CHANGE THE LOCATIONS OF THE INPUTS AND OUTPUTS!
  //   These are DEBUG/TEST outputs from your circuit.
  //   OUTPUTS from your circuit
endmodule
